# Fritzing sketch NodeBoard (saved by Fritzing 0.9.3b)
circuit board: 8.46667cm x 5.64444cm
breadboards: 1

parts:
  Part1 = Arduino Nano (Rev3.0)
  DHT1 = DHT22 Humidity and Temperature Sensor [part_number=DHT22]
  Part2 = OLED Monochrome 128x32 I2C [part_number=931]
  Part3 = Adafruit TSL2561 [part_number="Adafruit #439"]
  Part4 = NRF24L01

nets:
  GND: Part1.GND, DHT1.GND, Part2.GND, Part3.GND, Part4.GND
  N1: Part1.D2, DHT1.DATA
  N2: Part1.D9, Part4.CSN
  N3: Part1.D10, Part4.CE
  N4: Part1.D11/MOSI, Part4.MOSI
  N5: Part1.D12/MISO, Part4.MISO
  3.3V: Part1.5V, DHT1.VDD, Part2.3.3V, Part3.3.3V
  N6: Part1.A5, Part2.SCL, Part3.SCL
  N7: Part1.A4, Part2.SDA, Part3.SDA
  3V3: Part1.3V3, Part4.VCC
  N8: Part1.D13/SCK, Part4.SCK

custom parts:
  OLED Monochrome 128x32 I2C: These displays are small, only about 1" diagonal, but very readable due to the high contrast of an OLED display. This display is made of 128x32 individual white OLED pixels, each one is turned on or off by the controller chip. Because the display makes its own light, no backlight is required. This reduces the power required to run the OLED and is why the display has such high contrast; we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
  Adafruit TSL2561: The TSL2561 luminosity sensor is an advanced digital light sensor, ideal for use in a wide range of light situations. Compared to low cost CdS cells, this sensor is more precise, allowing for exact lux calculations and can be configured for different gain/timing ranges to detect light ranges from up to 0.1 - 40,000+ Lux on the fly. The best part of this sensor is that it contains both infrared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
